# Fritzing sketch Password (saved by Fritzing 0.9.2b)
circuit board: 9.46568cm x 3.74862cm
breadboards: 1

parts:
  X1 = USB Connectors [package=usb-a-h]
  U1 = 7-SEGMENT-4DIGIT-YOUNGSUN [package=7-segment-4digit-youngsun-longpads]
  R4 = Resistor [tolerance=±5% resistance=3.65k package=THT]
  D2 = Zener Diode [part_number=1N4732A breakdown_voltage=3.6V package="300 mil [THT]"]
  R6 = Resistor [tolerance=±5% resistance=3.65k package=THT]
  D1 = Zener Diode [part_number=1N4732A breakdown_voltage=3.6V package="300 mil [THT]"]
  IC1 = ATTiny2313 [part_number="ATtiny 2313" package=THT]
  XTAL1 = Crystal [frequency="16 MHz" part_number=12MHz package=THT]
  C1 = Ceramic Capacitor [capacitance=100nF voltage=6.3V part_number=27nF package="100 mil [THT, multilayer]"]
  S1 = Round Pushbutton
  Q1 = PNP-Transistor [part_number=BC327 package="TO92 [THT]"]
  Q2 = PNP-Transistor [part_number=BC327 package="TO92 [THT]"]
  Q3 = PNP-Transistor [part_number=BC327 package="TO92 [THT]"]
  Q4 = PNP-Transistor [part_number=BC327 package="TO92 [THT]"]
  R5 = Resistor [tolerance=±5% resistance=3.65k package=THT]
  R10 = Resistor [tolerance=±5% resistance=68 package=THT]
  R11 = Resistor [tolerance=±5% resistance=1.5k package=THT]
  R7 = Resistor [tolerance=±5% resistance=3.65k package=THT]
  R9 = Resistor [tolerance=±5% resistance=68 package=THT]
  C2 = Ceramic Capacitor [capacitance=100nF part_number=27nF package="100 mil [THT, multilayer]"]
  IC3 = ULN2803A [package=THT]

nets:
  N1: X1.D-, D2.cathode, R10.Pin_1, R11.Pin_0
  N2: X1.D+, D1.cathode, R9.Pin_1
  5V: X1.VBUS, IC1.VCC, Q1.E, Q2.E, Q3.E, Q4.E, R11.Pin_1
  GND: X1.GND, D2.anode, D1.anode, IC1.GND, C1.1, S1.leg1, C2.1, IC3.0V
  N3: U1.DIG1, Q1.C
  N4: U1.DIG2, Q2.C
  N5: U1.D, IC3.Out_1
  N6: U1.E, IC3.Out_2
  N7: U1.DIG3, Q3.C
  N8: U1.DP, IC3.Out_8
  N9: U1.DIG4, Q4.C
  N10: U1.F, IC3.Out_3
  N11: U1.C, IC3.Out_4
  N12: U1.A, IC3.Out_5
  N13: U1.G, IC3.Out_6
  N14: U1.B, IC3.Out_7
  N15: R4.Pin_0, IC1.PD6
  N16: R4.Pin_1, Q1.B
  N17: R6.Pin_0, IC1.PD1
  N18: R6.Pin_1, Q3.B
  N19: IC1.PD0, R5.Pin_0
  N20: IC1.PA1, XTAL1.pin_1, C1.0
  N21: IC1.PA0, XTAL1.pin_0, C2.0
  N22: IC1.PD2, R9.Pin_0
  N23: IC1.PD3, R10.Pin_0
  N24: IC1.PD4, R7.Pin_0
  N25: IC1.PD5, S1.leg0
  N26: IC1.PB0, IC3.In_8
  N27: IC1.PB1, IC3.In_7
  N28: IC1.PB2, IC3.In_6
  N29: IC1.PB3, IC3.In_5
  N30: IC1.PB4, IC3.In_4
  N31: IC1.PB5, IC3.In_3
  N32: IC1.PB6, IC3.In_2
  N33: IC1.PB7, IC3.In_1
  N34: Q2.B, R5.Pin_1
  N35: Q4.B, R7.Pin_1

notes:
  Password Storage, A deniable storage for 16 passwords with hardware PIN and USB-HID, 1
  Password Store

custom parts:
  ULN2803A: ULN2803A 8-way Darlington Transistor Driver
